// Logisim project 4-bit Full Adder with Hex Displayer.circ as structural Verilog: 1 circuit, main circuit main
module main (
  input  m,
  input  [3:0] a,
  input  [3:0] b,
  input  in_4
);

  wire adder_1_cout, adder_2_cout, adder_3_cout, xor_1_out, xor_2_out, xor_3_out, xor_4_out;
  wire [0:0] adder_4_cout;
  wire [3:0] adder_1_out;

  xor xor_1 (xor_1_out, b[0], m);
  xor xor_2 (xor_2_out, b[1], m);
  xor xor_3 (xor_3_out, b[2], m);
  xor xor_4 (xor_4_out, b[3], m);
  Adder #(.width(1)) adder_1 (.a(xor_1_out), .b(a[0]), .out(adder_1_out[0]), .cin(m), .cout(adder_1_cout));
  Adder #(.width(1)) adder_2 (.a(xor_2_out), .b(a[1]), .out(adder_1_out[1]), .cin(adder_1_cout), .cout(adder_2_cout));
  Adder #(.width(1)) adder_3 (.a(xor_3_out), .b(a[2]), .out(adder_1_out[2]), .cin(adder_2_cout), .cout(adder_3_cout));
  Adder #(.width(1)) adder_4 (
    .a(xor_4_out), .b(a[3]), .out(adder_1_out[3]), .cin(adder_3_cout), .cout(adder_4_cout[0]));
  Hex_Digit_Display hex_digit_display_1 (.value({{3{in_4}}, adder_4_cout[0]}));  // open: dp
  Hex_Digit_Display hex_digit_display_2 (.value(adder_1_out));  // open: dp
endmodule
