// Logisim project 7 Segment displayer.circ as structural Verilog: 2 circuits, main circuit main
module main (
  input  a,
  input  b,
  input  c,
  input  d,
  output x,
  output y,
  output z,
  output u,
  output v,
  output w,
  output s
);

  wire and_1_out, and_2_out, and_3_out, and_4_out, and_5_out, and_6_out, and_7_out, and_8_out, and_9_out,
       and_10_out, and_11_out, and_12_out, and_13_out, and_14_out, and_15_out, and_16_out, not_1_out,
       not_2_out, not_3_out, not_4_out, not_5_out, not_6_out, not_7_out, not_8_out, not_9_out, not_10_out,
       not_11_out, not_12_out, not_13_out, not_14_out, not_15_out, not_16_out, not_17_out, not_18_out,
       not_19_out, not_20_out, not_21_out;

  not not_1 (not_1_out, b);
  and and_1 (and_1_out, not_1_out, not_2_out);
  not not_2 (not_2_out, d);
  and and_2 (and_2_out, b, d);
  not not_3 (not_3_out, b);
  not not_4 (not_4_out, c);
  and and_3 (and_3_out, not_4_out, not_5_out);
  not not_5 (not_5_out, d);
  and and_4 (and_4_out, c, d);
  not not_6 (not_6_out, c);
  or or_1 (z, not_6_out, d, b);
  not not_7 (not_7_out, b);
  and and_5 (and_5_out, not_7_out, not_8_out);
  not not_8 (not_8_out, d);
  not not_9 (not_9_out, b);
  and and_6 (and_6_out, not_9_out, c);
  and and_7 (and_7_out, c, not_10_out);
  not not_10 (not_10_out, d);
  and and_8 (and_8_out, b, not_11_out, d);
  not not_11 (not_11_out, c);
  not not_12 (not_12_out, b);
  and and_9 (and_9_out, not_12_out, not_13_out);
  not not_13 (not_13_out, d);
  and and_10 (and_10_out, c, not_14_out);
  not not_14 (not_14_out, d);
  not not_15 (not_15_out, c);
  and and_11 (and_11_out, not_15_out, not_16_out);
  not not_16 (not_16_out, d);
  and and_12 (and_12_out, b, not_17_out);
  not not_17 (not_17_out, c);
  and and_13 (and_13_out, b, not_18_out);
  not not_18 (not_18_out, d);
  not not_19 (not_19_out, b);
  and and_14 (and_14_out, not_19_out, c);
  and and_15 (and_15_out, b, not_20_out);
  not not_20 (not_20_out, c);
  and and_16 (and_16_out, b, not_21_out);
  not not_21 (not_21_out, d);
  or or_2 (x, and_1_out, c, and_2_out, a);
  or or_3 (y, not_3_out, and_3_out, and_4_out);
  or or_4 (u, and_5_out, and_6_out, and_7_out, and_8_out, a);
  or or_5 (v, and_9_out, and_10_out);
  or or_6 (w, and_11_out, and_12_out, and_13_out, a);
  or or_7 (s, and_14_out, and_15_out, and_16_out, a);
endmodule

module _7_segmnent (
  input  [3:0] in_1
);

  wire main_1_s, main_1_u, main_1_v, main_1_w, main_1_x, main_1_y, main_1_z;

  main main_1 (
    .a(in_1[3]), .b(in_1[2]), .c(in_1[1]), .d(in_1[0]), .x(main_1_x), .y(main_1_y), .z(main_1_z),
    .u(main_1_u), .v(main_1_v), .w(main_1_w), .s(main_1_s));
  _7_Segment_Display u_7_segment_display_1 (
    .g(main_1_s), .f(main_1_w), .a(main_1_x), .b(main_1_y), .e(main_1_v), .d(main_1_u), .c(main_1_z));  // open: dp
endmodule
