// Logisim project 3x8 Decoder.circ as structural Verilog: 3 circuits, main circuit Decoder
module Decoder (
  input  x,
  input  y,
  input  z,
  input  E,
  output D0,
  output D1,
  output D2,
  output D3,
  output D4,
  output D5,
  output D6,
  output D7
);

  wire xn, yn, zn;

  not not_1 (xn, x);
  not not_2 (yn, y);
  not not_3 (zn, z);
  and x_prime_y_prime_z_prime (D0, xn, yn, zn, E);
  and x_prime_y_prime_z (D1, xn, yn, z, E);
  and x_prime_yz_prime (D2, xn, y, zn, E);
  and x_prime_yz (D3, xn, y, z, E);
  and xy_prime_z_prime (D4, x, yn, zn, E);
  and xy_prime_z (D5, x, yn, z, E);
  and xyz_prime (D6, x, y, zn, E);
  and xyz (D7, x, y, z, E);
endmodule

module Adder (
  input  A,
  input  Cin,
  input  e,
  input  B,
  output cOut,
  output Sum
);

  wire decoder_1_d1, decoder_1_d2, decoder_1_d3, decoder_1_d4, decoder_1_d5, decoder_1_d6, decoder_1_d7;

  Decoder decoder_1 (
    .x(A), .y(B), .z(Cin), .E(e), .D1(decoder_1_d1), .D2(decoder_1_d2), .D3(decoder_1_d3), .D4(decoder_1_d4),
    .D5(decoder_1_d5), .D6(decoder_1_d6), .D7(decoder_1_d7));  // open: D0
  or or_1 (Sum, decoder_1_d1, decoder_1_d2, decoder_1_d4, decoder_1_d7);
  or or_2 (cOut, decoder_1_d7, decoder_1_d6, decoder_1_d3, decoder_1_d5);
endmodule

module _5x32 (
  input  A0,
  input  A1,
  input  A2,
  input  A3,
  input  A4
);

  wire and_1_out, and_2_out, and_3_out, and_4_out, not_1_out, not_2_out;

  not not_1 (not_1_out, A3);
  and and_1 (and_1_out, not_1_out, not_2_out);
  and and_2 (and_2_out, not_1_out, A4);
  not not_2 (not_2_out, A4);
  and and_3 (and_3_out, A3, not_2_out);
  and and_4 (and_4_out, A3, A4);
  Decoder decoder_1 (.x(A0), .y(A1), .z(A2), .E(and_1_out));  // open: D0, D1, D2, D3, D4, D5, D6, D7
  Decoder decoder_2 (.x(A0), .y(A0), .z(A2), .E(and_2_out));  // open: D0, D1, D2, D3, D4, D5, D6, D7
  Decoder decoder_3 (.x(A0), .y(A0), .z(A2), .E(and_3_out));  // open: D0, D1, D2, D3, D4, D5, D6, D7
  Decoder decoder_4 (.x(A0), .y(A0), .z(A2), .E(and_4_out));  // open: D0, D1, D2, D3, D4, D5, D6, D7
endmodule
